// Logisim project Cache_Architecture.circ as structural Verilog: 4 circuits, main circuit main
module main (
  input  [6:0] Data,
  input  Store,
  input  Load,
  input  [15:0] Address
);

  wire clock_1_out, not_1_out, Tag_Array_hit_miss;
  wire [6:0] block_array_1_data, Main_Memory_data_out, multiplexer_1_out;
  wire [9:0] Tag_Array_tag_output;

  Clock clock_1 (.out(clock_1_out));
  Tag_Array Tag_Array (
    .Clock(clock_1_out), .in_2(Address), .Store(Store), .Load(Load), .Hit_Miss(Tag_Array_hit_miss),
    .Tag_Output(Tag_Array_tag_output));
  Block_Array block_array_1 (
    .Location(Tag_Array_tag_output), .Write_Data(Data), .Enable(Tag_Array_hit_miss), .Clock(clock_1_out),
    .Store(Store), .Load(Load), .Data(block_array_1_data));
  not not_1 (not_1_out, Tag_Array_hit_miss);
  Memory Main_Memory (
    .Location(Address), .Write_Data(Data), .Store(Store), .Enable(not_1_out), .Clock(clock_1_out),
    .Load(Load), .Data_Out(Main_Memory_data_out));
  Multiplexer #(.width(7)) multiplexer_1 (
    .in0(block_array_1_data), .in1(Main_Memory_data_out), .out(multiplexer_1_out), .sel(not_1_out), .en(Load));
  TTY tty_1 (.data(multiplexer_1_out), .clk(clock_1_out));  // open: we, clr
endmodule

module Tag_Array (
  input  Clock,
  input  [15:0] in_2,
  input  Load,
  input  Store,
  output Hit_Miss,
  output [9:0] Tag_Output
);

  wire and_1_out, and_2_out, and_3_out, and_4_out, comparator_1_eq, comparator_2_eq, comparator_3_eq,
       comparator_4_eq, or_1_out, Ram_1, Ram_2, Ram_3, Ram_4;
  wire [8:8] and_5_out, and_6_out, and_7_out, and_8_out;
  wire [9:0] Data_1, Data_2, Data_3, Data_4, Tag_1, Tag_2, Tag_3, Tag_4;

  and and_1 (and_1_out, Store, Ram_1);
  and and_2 (and_2_out, Store, Ram_2);
  and and_3 (and_3_out, Store, Ram_3);
  and and_4 (and_4_out, Store, Ram_4);
  or or_1 (or_1_out, Store, Load);
  RAM #(.addrWidth(5), .dataWidth(10), .bus("separate")) u_ram_1 (
    .addr(in_2[7:3]), .din(Data_1), .data(Tag_1), .str(and_1_out), .clk(Clock), .ld(or_1_out));  // open: sel, clr
  RAM #(.addrWidth(5), .dataWidth(10), .bus("separate")) u_ram_2 (
    .addr(in_2[7:3]), .din(Data_2), .data(Tag_2), .str(and_2_out), .clk(Clock), .ld(or_1_out));  // open: sel, clr
  RAM #(.addrWidth(5), .dataWidth(10), .bus("separate")) u_ram_3 (
    .addr(in_2[7:3]), .din(Data_3), .data(Tag_3), .str(and_3_out), .clk(Clock), .ld(or_1_out));  // open: sel, clr
  RAM #(.addrWidth(5), .dataWidth(10), .bus("separate")) u_ram_4 (
    .addr(in_2[7:3]), .din(Data_4), .data(Tag_4), .str(and_4_out), .clk(Clock), .ld(or_1_out));  // open: sel, clr
  Comparator #(.mode("unsigned")) comparator_1 (.a(Tag_1[7:0]), .b(in_2[15:8]), .eq(comparator_1_eq));  // open: gt, lt
  and and_5 (and_5_out[8], comparator_1_eq, Tag_1[9]);
  Comparator #(.mode("unsigned")) comparator_2 (.a(Tag_2[7:0]), .b(in_2[15:8]), .eq(comparator_2_eq));  // open: gt, lt
  and and_6 (and_6_out[8], comparator_2_eq, Tag_2[9]);
  Comparator #(.mode("unsigned")) comparator_3 (.a(Tag_3[7:0]), .b(in_2[15:8]), .eq(comparator_3_eq));  // open: gt, lt
  and and_7 (and_7_out[8], comparator_3_eq, Tag_3[9]);
  Comparator #(.mode("unsigned")) comparator_4 (.a(Tag_4[7:0]), .b(in_2[15:8]), .eq(comparator_4_eq));  // open: gt, lt
  and and_8 (and_8_out[8], comparator_4_eq, Tag_4[9]);
  or u_Hit_Miss (Hit_Miss, and_5_out[8], and_6_out[8], and_7_out[8], and_8_out[8]);
  assign Data_1 = {1'b0, and_5_out[8], {8{1'b0}}} | Tag_1;  // OR_Gate or_2, 10 bits wide
  assign Data_2 = {1'b0, and_6_out[8], {8{1'b0}}} | Tag_2;  // OR_Gate or_3, 10 bits wide
  or or_4 (Tag_Output[3], and_6_out[8], and_8_out[8]);
  or or_5 (Tag_Output[4], and_7_out[8], and_8_out[8]);
  assign Data_3 = {1'b0, and_7_out[8], {8{1'b0}}} | Tag_3;  // OR_Gate or_6, 10 bits wide
  assign Data_4 = {1'b0, and_8_out[8], {8{1'b0}}} | Tag_4;  // OR_Gate or_7, 10 bits wide
  Decoder #(.select(2), .disabled(0)) decoder_1 (
    .out0(Ram_1), .out1(Ram_2), .out2(Ram_3), .out3(Ram_4), .sel(Tag_Output[4:3]), .en(Store));

  assign {Tag_Output[9:5], Tag_Output[2:0]} = in_2[7:0];

  // Other names for the same wires on the sheet: clk = Clock; Tag[7:0] = in_2[15:8]
endmodule

module Block_Array (
  input  [9:0] Location,
  input  [6:0] Write_Data,
  input  Enable,
  input  Clock,
  input  Store,
  input  Load,
  output [6:0] Data
);

  RAM #(.addrWidth(10), .dataWidth(7), .bus("separate")) ram_1 (
    .addr(Location), .din(Write_Data), .data(Data), .str(Store), .sel(Enable), .clk(Clock), .ld(Load));  // open: clr
endmodule

module Memory (
  input  [15:0] Location,
  input  [6:0] Write_Data,
  input  Clock,
  input  Store,
  input  Load,
  input  Enable,
  output [6:0] Data_Out
);

  RAM #(.addrWidth(16), .dataWidth(7), .bus("separate")) ram_1 (
    .addr(Location), .din(Write_Data), .data(Data_Out), .str(Store), .sel(Enable), .clk(Clock), .ld(Load));  // open: clr
endmodule
